# Fritzing sketch RC522 (saved by Fritzing 0.9.3b)
breadboards: 2

parts:
  元件1 = Arduino Uno (Rev3)
  元件2 = RFID USB Reader
  S1 = Pushbutton [package="[THT]"]
  J1 = Basic Servo
  J2 = Infrared Proximity Sensor
  D1 = LTE-302 [package=lte-302]
  R1 = Resistor [tolerance=±5% resistance=220 package="0603 [SMD]"]

nets:
  N1: 元件1.A0, J2.Vout
  N2: 元件1.A1, D1.C
  N3: 元件1.D8, J1.pulse
  N4: 元件1.D9_PWM, 元件2.GND
  N5: 元件1.D10_PWM/SS, 元件2.GNDT
  N6: 元件1.D11_PWM/MOSI, 元件2.ANT2
  N7: 元件1.D12/MISO, 元件2.ANT1
  N8: 元件1.D13/SCK, 元件2.CP
  GND: 元件1.GND, 元件1.D3_PWM, 元件2.TX-O, S1.Pin_3, S1.Pin_4, J1.gnd, J2.GND, D1.A, R1.Pin_0, R1.Pin_1
  N9: 元件1.D2, 元件2.TX-O-RS232
  3V3: 元件1.3V3, 元件2.VCC
  VCC: 元件1.5V, J1.vcc, J2.Vcc
  N10: S1.Pin_1, S1.Pin_2
